# Fritzing sketch SeedOledV11_I2C (saved by Fritzing 0.9.4)

parts:
  J1 = longpad pin header, 6 pins [form="long pad"]
  J2 = longpad pin header, 6 pins [form="long pad"]
  J3 = longpad pin header, 6 pins [form="long pad"]  # not connected
  J4 = longpad pin header, 6 pins [form="long pad"]  # not connected
  J5 = longpad pin header, 7 pins [form="long pad"]  # not connected
  J6 = longpad pin header, 7 pins [form="long pad"]  # not connected
  J7 = longpad pin header, 7 pins [form="long pad"]  # not connected
  J8 = longpad pin header, 7 pins [form="long pad"]  # not connected
  Grove1 = Grove OLED 128x96

nets:
  N1: J1.pin1, Grove1.GND
  N2: J2.pin2, Grove1.VCC
  N3: J2.pin4, Grove1.SCL
  N4: J2.pin5, Grove1.SDA
